# Fritzing sketch fan_ctrl_with_led (saved by Fritzing 0.9.10b)
breadboards: 1

parts:
  Pico_H1 = Raspberry Pi Pico H
  R2 = Resistor [tolerance=±5% power=0.25 resistance=10k package=THT]
  Q1 = NPN-Transistor [part_number=S8050 package="SOT-23 [SMD]"]
  R3 = Resistor [tolerance=±5% power=0.25 resistance=1k package=THT]
  R1 = Temperature Sensor (Thermistor) [thermistor_type=NTC package=THT]
  J1 = Power Jack [package=power_jack_slot]
  F1 = Fan - 4 wire [package=THT]
  D1 = Diode [part_number=1n4007 package=diode-1n4001]
  Part1 = LCD1602-I2C

nets:
  GND: Pico_H1.GND, Q1.2, R1.pin_1, J1.GND, Part1.GND
  3V3: Pico_H1.3V3, R2.Pin_1, Part1.VCC
  N1: Pico_H1.GP28_A2, R2.Pin_0, R1.pin_0
  N2: Pico_H1.GP6, R3.Pin_0
  N3: Pico_H1.GP5, Part1.SCL
  N4: Pico_H1.GP4, Part1.SDA
  N5: Q1.0, R3.Pin_1
  N6: Q1.1, F1.GND, D1.A
  N7: J1.PWR, F1.Power, D1.C

custom parts:
  Raspberry Pi Pico H: Raspberry Pi Pico H. Based around the RP2040 microcontroller the Pico H is a low cost microcontroller device bringing Raspberry Pi quality, cost, and easy of use to the microcontroller space.
  Fan - 4 wire: Fan, 4 wire with tach.
  LCD1602-I2C: A standard character display, usually with 2x16 characters. Comes in many colors with LCM1602 IIC attached.
